# Fritzing sketch frtizing-diagram (saved by Fritzing 0.9.2b)
breadboards: 1

parts:
  Part1 = Photon
  neopixel1 = Neopixel 24 Ring
  ENCODER1 = Rotary Encoder with Knob
  OLED1 = 128x64 Monochrom OLED Display with SPI Control

nets:
  N1: Part1.A2, OLED1.CS
  GND: Part1.GND, neopixel1.GND, ENCODER1.no_name_yet#2, OLED1.GND
  VIN: Part1.VIN, neopixel1.Vcc
  N2: Part1.D2, ENCODER1.no_name_yet#1
  N3: Part1.D3, ENCODER1.no_name_yet#3
  N4: Part1.D4, ENCODER1.no_name_yet#4
  N5: Part1.D5, neopixel1.IN
  N6: Part1.D6, OLED1.SA0/DC
  N7: Part1.D7, OLED1.Reset
  3V3: Part1.3V3, ENCODER1.no_name_yet#5, OLED1.3v3

notes:
  Battery Shield

custom parts:
  Rotary Encoder with Knob: Rotary Encoder with 1/4" Shaft and Knob
